# Fritzing sketch Semaforo (saved by Fritzing 0.9.3b)
breadboards: 1

parts:
  LED1 = LED - 5mm [color="Red (633nm)" package="5 mm [THT]"]
  Componente1 = Arduino Uno (Rev3)
  R1 = Resistor [tolerance=±5% resistance=330 package=THT]
  LED2 = LED - 5mm [color="Yellow (595nm)" package="5 mm [THT]"]
  LED3 = LED - 5mm [color="Green (555nm)" package="5 mm [THT]"]
  R2 = Resistor [tolerance=±5% resistance=330 package=THT]
  R3 = Resistor [tolerance=±5% resistance=330 package=THT]

nets:
  N1: LED1.cathode, Componente1.GND, LED2.cathode, LED3.cathode
  N2: LED1.anode, R3.Pin_0
  N3: Componente1.D3_PWM, R3.Pin_1
  N4: Componente1.D4, R2.Pin_1
  N5: Componente1.D5_PWM, R1.Pin_1
  N6: R1.Pin_0, LED3.anode
  N7: LED2.anode, R2.Pin_0

// code stored in the sketch: Untitled.ino
int Rosso = 3;
int Giallo = 4;
int Verde = 5;
int Puls = 6;
int Rosso2 = 7;
int Giallo2 = 8;
int Verde2 = 9;

void Macchine();
void Pedoni();

void setup() 
{
  pinMode(Rosso, OUTPUT);
  pinMode(Giallo, OUTPUT);
  pinMode(Verde, OUTPUT);
  pinMode(Rosso2, OUTPUT);
  pinMode(Giallo2, OUTPUT);
  pinMode(Verde2, OUTPUT);
  pinMode(Puls, INPUT);
  
}

void loop() 
{
  Macchine();
}

void Pedoni()
{
  digitalWrite(Rosso, HIGH);
  digitalWrite(Verde2, HIGH);
  delay(3000);
  digitalWrite(Verde2, LOW);
  
  digitalWrite(Giallo2, HIGH);
  delay(1500);
  digitalWrite(Giallo2, LOW);
  
  digitalWrite(Rosso2, HIGH);
  delay(3000);
  digitalWrite(Rosso2, LOW);
  digitalWrite(Rosso, LOW);
}
void Macchine()
{
  digitalWrite(Verde, HIGH);
  
  delay(4000);
  
  digitalWrite(Giallo, HIGH);
  
  delay(1000);
  
  digitalWrite(Giallo, LOW);
  digitalWrite(Verde, LOW);

  digitalWrite(Rosso, HIGH);
 
  delay(5000);

  digitalWrite(Rosso, LOW);

}
